// Logisim project 8080.circ as structural Verilog: 45 circuits, main circuit PC-8080
module PC_8080 (
);

  wire Reset_out;
  wire [7:0] keyboard_1_data;
  wire [11:0] undriven;

  Button Reset (.out(Reset_out));
  System system_1 (.ResetIn(Reset_out));
  TTY #(.rows(25), .cols(80)) tty_1 (.data(undriven[6:0]), .clk(undriven[7]), .we(undriven[8]), .clr(undriven[9]));
  Keyboard keyboard_1 (
    .clk(undriven[7]), .re(undriven[10]), .clr(undriven[11]), .avail(keyboard_1_data[7]),
    .data(keyboard_1_data[6:0]));

  // Notes on the sheet:
  //   Key Input
endmodule

module System (
  input  ResetIn
);

  wire CLK, decoder_1_out0, decoder_1_out1, decoder_1_out2, decoder_1_out3, IRQ, n8080_core_1_p5,
       n8080_core_1_p7, n8080_core_1_p11, n8080_core_1_p13, not_1_out;
  wire [7:0] n8080_core_1_p9;
  wire [9:0] counter_1_q;
  wire [15:0] n8080_core_1_p12;

  Clock Clock (.out(CLK));
  Counter #(.width(10), .max('h3ff)) counter_1 (.Q(counter_1_q), .clk(CLK));  // open: load, D, count, carry, clr
  Pull_Resistor #(.pull(1)) pull_resistor_1 (.node(IRQ));
  LED led_1 (.in(counter_1_q[8]));
  // _8080_Core 8080_core_1: pin names not known; wires that end beside it: counter_1_q[8], CLK, ResetIn, IRQ, n8080_core_1_p5, n8080_core_1_p5, n8080_core_1_p7, n8080_core_1_p7, n8080_core_1_p9, n8080_core_1_p9, n8080_core_1_p11, n8080_core_1_p12, n8080_core_1_p13
  // Probe on n8080_core_1_p12
  // Probe on n8080_core_1_p9
  Pull_Resistor #(.pull(1)) pull_resistor_2 (.node(n8080_core_1_p13));
  Pull_Resistor #(.pull(1)) pull_resistor_3 (.node(n8080_core_1_p11));
  Pull_Resistor #(.pull(1)) pull_resistor_4 (.node(n8080_core_1_p9));
  Pull_Resistor pull_resistor_5 (.node(n8080_core_1_p12));
  not not_1 (not_1_out, n8080_core_1_p13);
  Decoder_part #(.select(2), .disabled(0), .enable("false")) decoder_1 (
    .out0(decoder_1_out0), .out1(decoder_1_out1), .out2(decoder_1_out2), .out3(decoder_1_out3),
    .sel(n8080_core_1_p12[15:14]));
  ROM #(.addrWidth(14)) rom_1 (.addr(n8080_core_1_p12[13:0]), .data(n8080_core_1_p9), .sel(decoder_1_out0));
  RAM #(.addrWidth(14)) ram_1 (
    .addr(n8080_core_1_p12[13:0]), .data(n8080_core_1_p9), .sel(decoder_1_out1), .clk(not_1_out),
    .ld(n8080_core_1_p11), .clr(1'b0));
  RAM #(.addrWidth(14)) ram_2 (
    .addr(n8080_core_1_p12[13:0]), .data(n8080_core_1_p9), .sel(decoder_1_out2), .clk(not_1_out),
    .ld(n8080_core_1_p11), .clr(1'b0));
  RAM #(.addrWidth(14)) ram_3 (
    .addr(n8080_core_1_p12[13:0]), .data(n8080_core_1_p9), .sel(decoder_1_out3), .clk(not_1_out),
    .ld(n8080_core_1_p11), .clr(1'b0));

  // Other names for the same wires on the sheet: Reset = ResetIn

  // Notes on the sheet:
  //   ROM0
  //   RAM0
  //   contents of rom_1 (hex, n*v repeats v):
  //   60 68 0 7b 0 7d 1f 0 5 bf e5 4 d7 fe 2 0 ee fe 7c 0 f 0 a5 8 e5 fb d6 9 fe e9 ff 48 65 6c 6c 6f 0 6e
  //   48 65 6c 6c 6f 43*0 76 1199*0 76 2553*0 f8 aa 8478*0 6e
  //   RAM1
  //   RAM2
endmodule

module XORSHIFT (
  input  CLK,
  output [7:0] RND
);

  wire Initialize, not_1_out, not_2_out, not_3_out, not_4_out, not_5_out, not_6_out, not_7_out, not_8_out,
       not_9_out, not_10_out, not_11_out, not_12_out, not_13_out, not_14_out, not_15_out, not_16_out;
  wire [7:0] T_q;
  wire [12:0] W_q_2;
  wire [18:0] W_q;
  wire [23:0] T_q_2;
  wire [31:0] multiplexer_1_out, multiplexer_2_out, multiplexer_3_out, multiplexer_4_out, X_q, xor_1_out,
       xor_2_out, xor_3_out, Y_q, Z_q;
  wire [31:8] xor_4_out;

  Register #(.width(1)) register_1 (.D(1'b1), .en(1'b1), .Q(Initialize), .clk(CLK), .clr(1'b0));
  Multiplexer #(.width(32)) multiplexer_1 (
    .in0(32'h1f123bb5), .in1({W_q_2, W_q}), .out(multiplexer_1_out), .sel(Initialize), .en(1'b1));
  not not_1 (not_1_out, CLK);
  not not_2 (not_2_out, not_1_out);
  Register #(.width(32)) Z (.D(multiplexer_1_out), .en(1'b1), .Q(Z_q), .clk(not_2_out), .clr(1'b0));
  Multiplexer #(.width(32)) multiplexer_2 (
    .in0(32'h159a55e5), .in1(Z_q), .out(multiplexer_2_out), .sel(Initialize), .en(1'b1));
  Register #(.width(32), .trigger("falling")) Y (
    .D(multiplexer_2_out), .en(1'b1), .Q(Y_q), .clk(not_3_out), .clr(1'b0));
  not not_3 (not_3_out, CLK);
  Multiplexer #(.width(32)) multiplexer_3 (
    .in0(32'h75bcd15), .in1(Y_q), .out(multiplexer_3_out), .sel(Initialize), .en(1'b1));
  Register #(.width(32)) X (.D(multiplexer_3_out), .en(1'b1), .Q(X_q), .clk(CLK), .clr(1'b0));
  assign xor_1_out = X_q ^ {X_q[20:0], {11{1'b0}}};  // XOR_Gate xor_1, 32 bits wide
  not not_4 (not_4_out, not_6_out);
  not not_5 (not_5_out, not_4_out);
  not not_6 (not_6_out, not_8_out);
  not not_7 (not_7_out, not_5_out);
  not not_8 (not_8_out, not_9_out);
  not not_9 (not_9_out, not_10_out);
  not not_10 (not_10_out, not_11_out);
  not not_11 (not_11_out, not_12_out);
  not not_12 (not_12_out, not_13_out);
  not not_13 (not_13_out, CLK);
  Register #(.width(32)) T (.D(xor_1_out), .en(1'b1), .Q({T_q_2, T_q}), .clk(not_7_out), .clr(1'b0));
  Multiplexer #(.width(32)) multiplexer_4 (
    .in0(32'h5491333), .in1({xor_4_out, RND}), .out(multiplexer_4_out), .sel(Initialize), .en(1'b1));
  assign xor_2_out = {T_q_2, T_q} ^ {{8{1'b0}}, T_q_2};  // XOR_Gate xor_2, 32 bits wide
  not not_14 (not_14_out, not_15_out);
  not not_15 (not_15_out, CLK);
  Register #(.width(32), .trigger("falling")) W (
    .D(multiplexer_4_out), .en(1'b1), .Q({W_q_2, W_q}), .clk(not_16_out), .clr(1'b0));
  not not_16 (not_16_out, not_14_out);
  assign xor_3_out = {W_q_2, W_q} ^ {{19{1'b0}}, W_q_2};  // XOR_Gate xor_3, 32 bits wide
  // Probe on {xor_4_out, RND}
  assign {xor_4_out, RND} = xor_3_out ^ xor_2_out;  // XOR_Gate xor_4, 32 bits wide

  // Notes on the sheet:
  //   負論理：シミュレーションがリセットされたあと最初の
  //   クロックでレジスタに初期値をロードする
endmodule

module Equal14 (
  input  [13:0] In0,
  input  [13:0] In1,
  output Y
);

  wire [13:0] not_1_out, xor_1_out;

  assign not_1_out = ~xor_1_out;  // NOT_Gate not_1, 14 bits wide
  assign xor_1_out = In0 ^ In1;  // XOR_Gate xor_1, 14 bits wide
  and and_1 (Y, not_1_out[0], not_1_out[1], not_1_out[2], not_1_out[3], not_1_out[4], not_1_out[5], not_1_out[6], not_1_out[7], not_1_out[8], not_1_out[9], not_1_out[10], not_1_out[11], not_1_out[12], not_1_out[13]);
endmodule

module _8080_Core (
  input  [7:0] DataIn,
  input  nIRQ,
  input  CLK,
  input  Reset,
  output [7:0] DataOut,
  output [15:0] AddressOut,
  output VMA,
  output nRST
);

  wire and_1_out, and_2_out, CLK_t, d_ff_1_q, d_ff_1_qn, d_ff_2_q, d_ff_3_q, not_1_out, not_2_out, not_3_out,
       not_4_out, not_5_out, not_7_out, P1, P2, PowerOnReset_q, xor_2_out;
  wire [3:0] counter_1_q;
  wire [7:0] executer_1_data_bus_out;
  wire [15:0] undriven;

  not not_1 (not_1_out, CLK);
  not not_2 (not_2_out, Reset);
  Counter #(.width(4), .max('hf)) counter_1 (
    .load(and_2_out), .D(4'b0011), .count(not_3_out), .Q(counter_1_q), .clk(CLK_t));  // open: carry, clr
  not not_3 (not_3_out, and_2_out);
  D_Flip_Flop d_ff_1 (.clk(not_1_out), .D(1'b0), .Q(d_ff_1_q), .Qn(d_ff_1_qn), .preset(not_4_out));  // open: en, reset
  not not_4 (not_4_out, and_1_out);
  D_Flip_Flop d_ff_2 (.clk(not_1_out), .D(d_ff_1_q), .Q(d_ff_2_q), .preset(not_5_out));  // open: Qn, en, reset
  not not_5 (not_5_out, and_1_out);
  and and_1 (and_1_out, not_2_out, PowerOnReset_q);
  D_Flip_Flop PowerOnReset (.clk(not_1_out), .D(1'b1), .Q(PowerOnReset_q));  // open: Qn, preset, en, reset
  and and_2 (and_2_out, counter_1_q[2], counter_1_q[3]);
  xor xor_1 (P2, counter_1_q[3], 1'b0);
  not not_6 (CLK_t, not_1_out);
  D_Flip_Flop d_ff_3 (.clk(not_1_out), .D(d_ff_2_q), .Q(d_ff_3_q), .preset(not_7_out));  // open: Qn, en, reset
  not not_7 (not_7_out, and_1_out);
  Executer executer_1 (
    .DATA_BUS_in(DataIn), .DATA_BUS_out(executer_1_data_bus_out), .ADDRESS_OUT(undriven), .P2(P2), .P1(P1),
    .nReset(nRST));  // open: HLTA, IRQ
  xor xor_2 (xor_2_out, counter_1_q[0], counter_1_q[1]);
  and and_3 (P1, xor_2_out, counter_1_q[2]);
  not not_8 (nRST, d_ff_3_q);
  assign AddressOut = 1'b1 ? undriven : 16'bz;  // Controlled_Buffer controlled_buffer_1
  assign DataOut = 1'b1 ? executer_1_data_bus_out : 8'bz;  // Controlled_Buffer controlled_buffer_2

  // Notes on the sheet:
  //   Reset: pull=up
  //   LogiSimのシミュレーションリセット対応
  //   DataBus
  //   AddressBus
endmodule

module Executer (
  input  [7:0] DATA_BUS_in,
  input  [15:0] ADDRESS_OUT,
  input  IRQ,
  input  P2,
  input  P1,
  input  nReset,
  output [7:0] DATA_BUS_out,
  output HLTA
);

  wire address_latch_1_out_6, timing_and_control_1_aluctrl;
  wire [4:0] alu_1_toflag, flag_1_toalu;
  wire [7:0] acc_1_monitor, acc_1_thru, acc_1_toact, act_1_monitor, act_1_toalu, address_latch_1_inc_dec_lo,
       databus_buffer_1_monitor, instructin_register_1_monitor, INTERNAL_DATABUS,
       multiplexer_1_toregister_array_lo, n8bitgpreg_h_1_ctrlout, n8bitgpreg_h_1_monitor,
       n8bitgpreg_h_1_todbus, n8bitgpreg_h_1_toincdec, n8bitgpreg_h_2_ctrlout, n8bitgpreg_h_2_monitor,
       n8bitgpreg_h_2_todbus, n8bitgpreg_h_2_toincdec, n8bitgpreg_h_3_ctrlout, n8bitgpreg_h_3_monitor,
       n8bitgpreg_h_3_todbus, n8bitgpreg_h_3_toincdec, n8bitgpreg_h_4_ctrlout, n8bitgpreg_h_4_monitor,
       n8bitgpreg_h_4_todbus, n8bitgpreg_h_4_toincdec, n8bitgpreg_h_5_ctrlout, n8bitgpreg_h_5_monitor,
       n8bitgpreg_h_5_todbus, n8bitgpreg_h_5_toincdec, n8bitgpreg_h_6_ctrlout, n8bitgpreg_h_6_monitor,
       n8bitgpreg_h_6_todbus, n8bitgpreg_h_6_toincdec, n8bitgpreg_l_1_monitor, n8bitgpreg_l_1_todbus,
       n8bitgpreg_l_1_toincdec, n8bitgpreg_l_2_monitor, n8bitgpreg_l_2_todbus, n8bitgpreg_l_2_toincdec,
       n8bitgpreg_l_3_monitor, n8bitgpreg_l_3_todbus, n8bitgpreg_l_3_toincdec, n8bitgpreg_l_4_monitor,
       n8bitgpreg_l_4_todbus, n8bitgpreg_l_4_toincdec, n8bitgpreg_l_5_monitor, n8bitgpreg_l_5_todbus,
       n8bitgpreg_l_5_toincdec, n8bitgpreg_l_6_monitor, n8bitgpreg_l_6_todbus, n8bitgpreg_l_6_toincdec,
       register_selector_1_bc_ctrl, register_selector_1_de_ctrl, register_selector_1_hl_ctrl,
       register_selector_1_pc_ctrl, register_selector_1_sp_ctrl, register_selector_1_wz_ctrl,
       temp_reg_1_monitor, temp_reg_1_toalu, undriven, undriven_2;
  wire [9:0] alu_1_todaa, decimal_adjust_1_toalu;
  wire [11:0] timing_and_control_1_accctrl;
  wire [15:0] address_latch_1_monitor, address_latch_1_monitor_2, address_latch_1_out,
       instructin_register_1_opecodeout, timing_and_control_1_aluctrl_2;
  wire [31:0] decoder_1_ctrlout, timing_and_control_1_ctrl;

  // Probe on acc_1_monitor
  // Probe on act_1_monitor
  ACC acc_1 (
    .fromDATA_BUS(INTERNAL_DATABUS), .ctrl(timing_and_control_1_accctrl), .toACT(acc_1_toact),
    .THRU(acc_1_thru), .Monitor(acc_1_monitor), .toDATA_BUS(INTERNAL_DATABUS));
  // Probe on temp_reg_1_monitor
  ACT act_1 (
    .fromAcc(acc_1_toact), .toALU(act_1_toalu), .AccTHRU(acc_1_thru), .ctrl(timing_and_control_1_accctrl),
    .Monitor(act_1_monitor));
  STATE_IND state_ind_1 ();  // open: State_in, out_2, out_3, out_4, out_5, out_6, out_7, out_8, out_9, out_10, out_11
  TEMP_REG temp_reg_1 (
    .fromDBUS(INTERNAL_DATABUS), .toALU(temp_reg_1_toalu), .ctrl(timing_and_control_1_accctrl),
    .monitor(temp_reg_1_monitor));
  TIMING_AND_CONTROL timing_and_control_1 (
    .AccCtrl(timing_and_control_1_accctrl), .P1(P1), .P2(P2), .ALUCtrl(timing_and_control_1_aluctrl),
    .nReset(nReset), .IRQ(IRQ), .ctrl(timing_and_control_1_ctrl), .ALUctrl_2(timing_and_control_1_aluctrl_2),
    .in_5(decoder_1_ctrlout));
  FLAG flag_1 (
    .toALU(flag_1_toalu), .fromALU(alu_1_toflag), .ctrl(timing_and_control_1_aluctrl_2),
    .fromDATABUS(INTERNAL_DATABUS), .toDATABUS(INTERNAL_DATABUS));
  ALU alu_1 (
    .S(timing_and_control_1_aluctrl_2), .B(temp_reg_1_toalu), .A(act_1_toalu), .ALU_OUT(INTERNAL_DATABUS),
    .toDAA(alu_1_todaa), .toFLAG(alu_1_toflag), .fromFLAG(flag_1_toalu), .fromDAA(decimal_adjust_1_toalu));
  DECIMAL_ADJUST decimal_adjust_1 (.fromALU(alu_1_todaa), .toALU(decimal_adjust_1_toalu));
  // Probe on databus_buffer_1_monitor
  // Probe on instructin_register_1_monitor
  INSTRUCTIN_REGISTER instructin_register_1 (
    .OPECODEin(INTERNAL_DATABUS), .OPECODEout(instructin_register_1_opecodeout),
    .ctrl(timing_and_control_1_ctrl), .monitor(instructin_register_1_monitor));
  Decoder decoder_1 (
    .DataIn(instructin_register_1_opecodeout), .ctrlOut(decoder_1_ctrlout), .ctrl(timing_and_control_1_ctrl));
  DATABUS_BUFFER databus_buffer_1 (
    .fromExDataBus(DATA_BUS_in), .toExDataBus(DATA_BUS_out), .toDataBus(INTERNAL_DATABUS),
    .fromDataBus(INTERNAL_DATABUS), .monitor(databus_buffer_1_monitor), .ctrl(timing_and_control_1_ctrl));
  REGISTER_SELECTOR register_selector_1 (
    .BC_Ctrl(register_selector_1_bc_ctrl), .DE_ctrl(register_selector_1_de_ctrl),
    .HL_ctrl(register_selector_1_hl_ctrl), .WZ_Ctrl(register_selector_1_wz_ctrl),
    .SP_ctrl(register_selector_1_sp_ctrl), .PC_ctrl(register_selector_1_pc_ctrl),
    .ctrl(timing_and_control_1_ctrl));
  _8BitGPReg_H u_8bitgpreg_h_1 (
    .Monitor(n8bitgpreg_h_1_monitor), .toDBUS(n8bitgpreg_h_1_todbus), .fromINCDEC(n8bitgpreg_h_2_todbus),
    .fromDBUS(undriven_2), .toINCDEC(n8bitgpreg_h_1_toincdec), .Control(register_selector_1_wz_ctrl),
    .ctrlOut(n8bitgpreg_h_1_ctrlout));  // open: out_7, out_8
  // Probe on n8bitgpreg_h_1_monitor
  _8BitGPReg_H u_8bitgpreg_h_2 (
    .Monitor(n8bitgpreg_h_2_monitor), .toDBUS(n8bitgpreg_h_2_todbus), .fromINCDEC(n8bitgpreg_h_3_todbus),
    .fromDBUS(n8bitgpreg_h_1_toincdec), .toINCDEC(n8bitgpreg_h_2_toincdec),
    .Control(register_selector_1_bc_ctrl), .ctrlOut(n8bitgpreg_h_2_ctrlout));  // open: out_7, out_8
  // Probe on n8bitgpreg_h_2_monitor
  _8BitGPReg_H u_8bitgpreg_h_3 (
    .Monitor(n8bitgpreg_h_3_monitor), .toDBUS(n8bitgpreg_h_3_todbus), .fromINCDEC(n8bitgpreg_h_4_todbus),
    .fromDBUS(n8bitgpreg_h_2_toincdec), .toINCDEC(n8bitgpreg_h_3_toincdec),
    .Control(register_selector_1_de_ctrl), .ctrlOut(n8bitgpreg_h_3_ctrlout));  // open: out_7, out_8
  // Probe on n8bitgpreg_h_3_monitor
  _8BitGPReg_H u_8bitgpreg_h_4 (
    .Monitor(n8bitgpreg_h_4_monitor), .toDBUS(n8bitgpreg_h_4_todbus), .fromINCDEC(n8bitgpreg_h_5_todbus),
    .fromDBUS(n8bitgpreg_h_3_toincdec), .toINCDEC(n8bitgpreg_h_4_toincdec),
    .Control(register_selector_1_hl_ctrl), .ctrlOut(n8bitgpreg_h_4_ctrlout));  // open: out_7, out_8
  // Probe on n8bitgpreg_h_4_monitor
  _8BitGPReg_H u_8bitgpreg_h_5 (
    .Monitor(n8bitgpreg_h_5_monitor), .toDBUS(n8bitgpreg_h_5_todbus), .fromINCDEC(n8bitgpreg_h_6_todbus),
    .fromDBUS(n8bitgpreg_h_4_toincdec), .toINCDEC(n8bitgpreg_h_5_toincdec),
    .Control(register_selector_1_sp_ctrl), .ctrlOut(n8bitgpreg_h_5_ctrlout));  // open: out_7, out_8
  // Probe on n8bitgpreg_h_5_monitor
  _8BitGPReg_H u_8bitgpreg_h_6 (
    .Monitor(n8bitgpreg_h_6_monitor), .toDBUS(n8bitgpreg_h_6_todbus), .fromINCDEC(undriven),
    .fromDBUS(n8bitgpreg_h_5_toincdec), .toINCDEC(n8bitgpreg_h_6_toincdec),
    .Control(register_selector_1_pc_ctrl), .ctrlOut(n8bitgpreg_h_6_ctrlout));  // open: out_7, out_8
  // Probe on n8bitgpreg_h_6_monitor
  // Probe on address_latch_1_monitor
  _8BitGPReg_L u_8bitgpreg_l_1 (
    .Monitor(n8bitgpreg_l_1_monitor), .toDBUS(n8bitgpreg_l_1_todbus),
    .fromDBUS(multiplexer_1_toregister_array_lo), .toINCDEC(n8bitgpreg_l_1_toincdec),
    .fromINCDEC(n8bitgpreg_l_2_todbus), .Control(n8bitgpreg_h_1_ctrlout));  // open: out_7, out_8
  // Probe on n8bitgpreg_l_1_monitor
  _8BitGPReg_L u_8bitgpreg_l_2 (
    .Monitor(n8bitgpreg_l_2_monitor), .toDBUS(n8bitgpreg_l_2_todbus), .fromDBUS(n8bitgpreg_l_1_toincdec),
    .toINCDEC(n8bitgpreg_l_2_toincdec), .fromINCDEC(n8bitgpreg_l_3_todbus), .Control(n8bitgpreg_h_2_ctrlout));  // open: out_7, out_8
  // Probe on n8bitgpreg_l_2_monitor
  _8BitGPReg_L u_8bitgpreg_l_3 (
    .Monitor(n8bitgpreg_l_3_monitor), .toDBUS(n8bitgpreg_l_3_todbus), .fromDBUS(n8bitgpreg_l_2_toincdec),
    .toINCDEC(n8bitgpreg_l_3_toincdec), .fromINCDEC(n8bitgpreg_l_4_todbus), .Control(n8bitgpreg_h_3_ctrlout));  // open: out_7, out_8
  // Probe on n8bitgpreg_l_3_monitor
  _8BitGPReg_L u_8bitgpreg_l_4 (
    .Monitor(n8bitgpreg_l_4_monitor), .toDBUS(n8bitgpreg_l_4_todbus), .fromDBUS(n8bitgpreg_l_3_toincdec),
    .toINCDEC(n8bitgpreg_l_4_toincdec), .fromINCDEC(n8bitgpreg_l_5_todbus), .Control(n8bitgpreg_h_4_ctrlout));  // open: out_7, out_8
  // Probe on n8bitgpreg_l_4_monitor
  _8BitGPReg_L u_8bitgpreg_l_5 (
    .Monitor(n8bitgpreg_l_5_monitor), .toDBUS(n8bitgpreg_l_5_todbus), .fromDBUS(n8bitgpreg_l_4_toincdec),
    .toINCDEC(n8bitgpreg_l_5_toincdec), .fromINCDEC(n8bitgpreg_l_6_todbus), .Control(n8bitgpreg_h_5_ctrlout));  // open: out_7, out_8
  // Probe on n8bitgpreg_l_5_monitor
  _8BitGPReg_L u_8bitgpreg_l_6 (
    .Monitor(n8bitgpreg_l_6_monitor), .toDBUS(n8bitgpreg_l_6_todbus), .fromDBUS(n8bitgpreg_l_5_toincdec),
    .toINCDEC(n8bitgpreg_l_6_toincdec), .fromINCDEC(address_latch_1_inc_dec_lo),
    .Control(n8bitgpreg_h_6_ctrlout));  // open: out_7, out_8
  // Probe on n8bitgpreg_l_6_monitor
  Pull_Resistor #(.pull(1)) pull_resistor_1 (.node(INTERNAL_DATABUS));
  MULTIPLEXER multiplexer_1 (
    .fromDATABUS(INTERNAL_DATABUS), .toDATABUS(INTERNAL_DATABUS),
    .toREGISTER_ARRAY_hi(n8bitgpreg_h_1_todbus), .fromREGISTER_ARRAY_hi(undriven_2),
    .ctrl(timing_and_control_1_ctrl), .toREGISTER_ARRAY_lo(multiplexer_1_toregister_array_lo),
    .fromREGISTER_ARRAY_lo(n8bitgpreg_l_1_todbus));
  // Probe on address_latch_1_monitor_2
  ADDRESS_LATCH address_latch_1 (
    .HI(undriven), .LO(n8bitgpreg_l_6_toincdec), .OUT(address_latch_1_out),
    .INC_DEC_HI(n8bitgpreg_h_6_toincdec), .INC_DEC_LO(address_latch_1_inc_dec_lo),
    .ctrl(timing_and_control_1_ctrl), .out_6(address_latch_1_out_6), .monitor_2(address_latch_1_monitor_2),
    .monitor(address_latch_1_monitor));
  ADDRESS_BUFFER address_buffer_1 (
    .in_1(address_latch_1_out), .out_3(ADDRESS_OUT), .ctrl(timing_and_control_1_aluctrl));
  // Probe on INTERNAL_DATABUS

  // Notes on the sheet:
  //   ACCUMRATOR
  //   ACCUMRATOR
  //   LATCH
  //   Figure 2-2 8080 CPU Functional Block Diagram
  //   TEMP. REG.
  //   DECIMAL
  //   ADJUST
  //   DATA BUS
  //   BUFFER/LATCH
  //   INSTRUCTION
  //   REGISTER
  //   W
  //   B
  //   D
  //   H
  //   SPH
  //   PCH
  //   MULTIPLEXER
  //   Z
  //   C
  //   E
  //   L
  //   SPL
  //   PCL
  //   REGISTER
  //   ARRAY
endmodule

module CLK_GEN (
  input  CLK,
  input  Reset,
  output Q,
  output nRST
);

  wire and_1_out, d_ff_1_q, d_ff_1_qn, d_ff_2_q, d_ff_3_q, not_1_out, not_2_out, not_3_out, not_4_out,
       not_5_out, PowerOnReset_q;

  not not_1 (not_1_out, CLK);
  not not_2 (not_2_out, Reset);
  D_Flip_Flop d_ff_1 (.clk(not_1_out), .D(1'b0), .Q(d_ff_1_q), .Qn(d_ff_1_qn), .preset(not_3_out));  // open: en, reset
  not not_3 (not_3_out, and_1_out);
  D_Flip_Flop PowerOnReset (.clk(not_1_out), .D(1'b1), .Q(PowerOnReset_q));  // open: Qn, preset, en, reset
  D_Flip_Flop d_ff_2 (.clk(not_1_out), .D(d_ff_1_q), .Q(d_ff_2_q), .preset(not_5_out));  // open: Qn, en, reset
  not not_4 (not_4_out, and_1_out);
  not not_5 (not_5_out, and_1_out);
  and and_1 (and_1_out, not_2_out, PowerOnReset_q);
  not not_6 (Q, not_1_out);
  D_Flip_Flop d_ff_3 (.clk(not_1_out), .D(d_ff_2_q), .Q(d_ff_3_q), .preset(not_4_out));  // open: Qn, en, reset
  not not_7 (nRST, d_ff_3_q);

  // Notes on the sheet:
  //   LogiSimのシミュレーションリセット対応
endmodule

module Decoder (
  input  [15:0] DataIn,
  input  [31:0] ctrl,
  output [31:0] ctrlOut
);

  wire ALUOPrM, ALUOPrr, and_8_out, and_9_out, block00, block01, block10, block11, CALLop, DAD,
       decoder_2_out0, decoder_2_out1, decoder_2_out2, decoder_2_out3, decoder_2_out4, decoder_2_out5,
       decoder_2_out6, decoder_2_out7, decoder_3_out0, decoder_3_out1, decoder_3_out2, decoder_3_out3,
       decoder_4_out0, decoder_4_out1, decoder_4_out2, decoder_4_out3, decoder_4_out4, decoder_4_out5,
       decoder_4_out6, decoder_4_out7, DoBranch, DST_M, HALT, JUMPop, MOVI_r, MOVMr, MOVrM, MOVrr,
       multiplexer_1_out, NOP, PM1OP_r, RETop, RST, SRC_M;

  Decoder_part #(.select(2), .disabled(0), .enable("false")) decoder_1 (
    .out0(block00), .out1(block01), .out2(block10), .out3(block11), .sel(DataIn[7:6]));
  and and_1 (SRC_M, ~DataIn[0], DataIn[1], DataIn[2]);  // AND_Gate
  and and_2 (DST_M, ~DataIn[3], DataIn[4], DataIn[5]);  // AND_Gate
  and and_3 (CALLop, ~DataIn[1], DataIn[2], block11);  // AND_Gate
  and and_4 (JUMPop, DataIn[1], ~DataIn[2], block11);  // AND_Gate
  and and_5 (RETop, ~DataIn[1], ~DataIn[2], block11);  // AND_Gate
  and and_6 (RST, DataIn[0], DataIn[1], DataIn[2], DataIn[6], DataIn[7]);
  nor nor_1 (NOP, DataIn[0], DataIn[1], DataIn[2], DataIn[6], DataIn[7]);
  and and_7 (PM1OP_r, block00, DataIn[1], ~DataIn[2]);  // AND_Gate
  and and_8 (and_8_out, block01, SRC_M);
  and and_9 (and_9_out, block01, DST_M);
  and and_10 (HALT, DST_M, SRC_M, block01);
  and and_11 (ALUOPrr, block10, ~SRC_M);  // AND_Gate
  and and_12 (ALUOPrM, block10, SRC_M);
  nor nor_2 (MOVrr, ~block01, and_8_out, and_9_out, HALT);  // NOR_Gate
  and and_13 (MOVrM, and_8_out, ~HALT);  // AND_Gate
  and and_14 (MOVMr, and_9_out, ~HALT);  // AND_Gate
  Multiplexer #(.select(2), .disabled(0), .enable("false")) multiplexer_1 (
    .in0(DataIn[14]), .in1(DataIn[8]), .in2(DataIn[10]), .in3(DataIn[15]), .out(multiplexer_1_out),
    .sel(DataIn[5:4]));
  xor xor_1 (DoBranch, multiplexer_1_out, ~DataIn[3]);  // XOR_Gate
  and and_15 (MOVI_r, block00, ~DataIn[0], DataIn[1], DataIn[2]);  // AND_Gate
  and and_16 (DAD, block00, DataIn[0], ~DataIn[1], ~DataIn[2], DataIn[3]);  // AND_Gate
  Decoder_part #(.select(3), .disabled(0), .enable("false")) decoder_2 (
    .out0(decoder_2_out0), .out1(decoder_2_out1), .out2(decoder_2_out2), .out3(decoder_2_out3),
    .out4(decoder_2_out4), .out5(decoder_2_out5), .out6(decoder_2_out6), .out7(decoder_2_out7),
    .sel(DataIn[5:3]));
  Decoder_part #(.select(2), .disabled(0), .enable("false")) decoder_3 (
    .out0(decoder_3_out0), .out1(decoder_3_out1), .out2(decoder_3_out2), .out3(decoder_3_out3),
    .sel(DataIn[5:4]));
  Decoder_part #(.select(3), .disabled(0), .enable("false")) decoder_4 (
    .out0(decoder_4_out0), .out1(decoder_4_out1), .out2(decoder_4_out2), .out3(decoder_4_out3),
    .out4(decoder_4_out4), .out5(decoder_4_out5), .out6(decoder_4_out6), .out7(decoder_4_out7),
    .sel(DataIn[2:0]));

  // Other names for the same wires on the sheet: ALU_OP[2:0] = DataIn[5:3]; Bits_Mid[2:0] = DataIn[5:3];
  //   DataIn_t[7:0] = DataIn[7:0]; DST_r[2:0] = DataIn[5:3]; RegX[1:0] = DataIn[5:4]; Bits_Lo[2:0] = DataIn[2:0];
  //   PM1OP_ｒ_DEC = DataIn[0]; SRC_r[2:0] = DataIn[2:0]; CY = DataIn[8]; FlagIn[7:0] = DataIn[15:8]; PF = DataIn[10];
  //   AC = DataIn[12]; ZF = DataIn[14]; SF = DataIn[15]

  // Notes on the sheet:
  //   _DECフラグは1の時DEC
  //   B
  //   C
  //   D
  //   E
  //   H
  //   L
  //   M
  //   A
  //   BC
  //   DE
  //   HL
  //   SP
  //   B
  //   C
  //   D
  //   E
  //   H
  //   L
  //   M
  //   A
endmodule

module uROM_B (
  input  [7:0] OpeCode,
  input  Load,
  input  Update,
  output [11:0] STEP_MON,
  output [31:0] CtrlSignal
);

  wire not_1_out;

  not not_1 (not_1_out, Load);
  Counter #(.width(4), .max('hf)) _161 (
    .load(Load), .D(4'b0000), .count(not_1_out), .Q(STEP_MON[3:0]), .clk(Update));  // open: carry, clr
  Register _377 (.D(OpeCode), .en(Load), .Q(STEP_MON[11:4]), .clk(Update));  // open: clr
  ROM #(.addrWidth(12), .dataWidth(32)) rom_1 (.addr(STEP_MON), .data(CtrlSignal));  // open: sel

  // Notes on the sheet:
  //   contents of rom_1 (hex, n*v repeats v):
  //   2402000c 80121300 2402000c 80123300 2402000c 80125300 2402000c 80127300 2402040c 80121300 2402040c
  //   80123300 2402040c 80125300 2402040c 80127300 3802000c 80020000 3802008c 80020000 3802010c 80020000
  //   3802018c 80020000 3802040c 80020000 3802048c 80020000 3802050c 80020000 3802058c 80020000 2402080c
  //   6db1c 24020304 80121300 2402080c 6db1c 24020304 80123300 2402080c 6db1c 24020304 80125300 2402080c
  //   6db1c 24020304 80127300 2402080c 6db1c 24020704 80121300 2402080c 6db1c 24020704 80123300 2402080c
  //   6db1c 24020704 80125300 2402080c 6db1c 24020704 80127300 2402080c 6db1c 38020004 80020000 2402080c
  //   6db1c 38020084 80020000 2402080c 6db1c 38020104 80020000 2402080c 6db1c 38020184 80020000 2402080c
  //   6db1c 38020404 80020000 2402080c 6db1c 38020484 80020000 2402080c 6db1c 38020504 80020000 2402080c
  //   6db1c 38020584 80020000 2402080c 6db1c 24020c04 80121300 2402080c 6db1c 24020c04 80123300 2402080c
  //   6db1c 24020c04 80125300 2402080c 6db1c 24020c04 80127300 2402040c 121300 2402041c 80123300 2402040c
  //   125300 2402041c 80127300 2402040c 121300 2402041c 80123300 2402040c 125300 2402041c 80127300
  //   2402080c 6db1c 38020c04 80020000 2402080c 6db1c 38020c84 80020000 2402080c 6db1c 38020d04 80020000
  //   2402080c 6db1c 38020d84 80020000 3802040c 20000 3802049c 80020000 3802050c 20000 3802059c 80020000
  //   3802040c 20000 3802049c 80020000 3802050c 20000 3802059c 17*80020000 80021100 80021180 80023100
  //   80023180 80025000 80025080 80027000 80027080 80021080 80023000 80025180 80027100 8002d00c 8002f00c
  //   8002d40c 8002f40c 21200 80023280 21600 80023680 23200 80025280 23600 80025680 60000 a0080 80029020
  //   60000 a0080 8002b020 60080 a0100 80029020 60080 a0100 8002b020 21200 80023280 21600 80023680 23200
  //   80025280 23600 80025680 80029800 80029c00 8002b800 8002bc00 2002fc08 18020000 20000 2002fc08
  //   18020080 80000000 2002fc08 18020200 20000 2002fc08 18020280 80000000 0 0 2002fc08 18020280 2002fc08
  //   18020200 80000000 2002fc08 18020680 2002fc08 18020600 80000000 2002fc08 18020a80 2002fc08 18020a00
  //   80000000 0 24020f0c 121f0c 2fc1c 24020f0c 123f0c 8002fc1c 24020f0c 125f0c 2fc1c 24020f0c 127f0c
  //   8002fc1c 260015 80203015 260115 80207015 24020c0c 6ff1c 24020c0c aff1c 80029020 24020c0c 6ff1c
  //   24020c0c aff1c 8002b020 24020c0c 6ff1c 24020c0c aff1c 8002d020 24020c0c 6ff1c 24020c0c aff1c
  //   8002f020 60000 a0080 80029000 60000 a0080 8002b400 60400 a0100 80029000 60400 a0100 8002b400 60000
  //   21100 425068 60080 23180 80427068 60200 a0280 2940c 8002b020 60000 a0080 25200 27280 80029020 60100
  //   a0180 25600 27680 8002b020 2402080c 121300 8002d81c 2402080c 123300 8002d81c 2402080c 125300
  //   8002d81c 2402080c 127300 8002d81c 2402080c 6db1c 2402080c adb1c 80029020 2402080c 6db1c 2402080c
  //   adb1c 8002b020 2402080c 6db1c 2402080c adb1c 8002d020 2402080c 6db1c 2402080c adb1c 8002f020 60000
  //   2a0033 80201033 60000 2a00b3 80201033 60000 2a0133 80201033 60000 2a01b3 80201033 60080 2a0033
  //   80203033 60080 24020800 adb1c 80201033 60080 2a0133 80203033 60080 2a01b3 80203033 60000 2a000e
  //   8020100e 60000 2a008e 8020100e 60000 2a010e 8020100e 60000 2a018e 8020100e 60080 2a000e 8020300e
  //   60080 24020800 adb1c 8020100e 60080 2a010e 8020300e 60080 2a018e 8020300e 60000 2a0030 80201030
  //   60000 2a00b0 80201030 60000 2a0130 80201030 60000 2a01b0 80201030 60080 2a0030 80203030 60080
  //   24020800 adb1c 80201030 60080 2a0130 80203030 60080 2a01b0 80203030 60000 2a000c 8020100c 60000
  //   2a008c 8020100c 60000 2a010c 8020100c 60000 2a018c 8020100c 60080 2a000c 8020300c 60080 24020800
  //   adb1c 8020100c 60080 2a010c 8020300c 60080 2a018c 8020300c 60000 4a0060 80401060 60000 4a00e0
  //   80401060 60000 4a0160 80401060 60000 4a01e0 80401060 60080 4a0060 80403060 60080 24020800 adb1c
  //   80401060 60080 4a0160 80403060 60080 4a01e0 80403060 60000 2a000e 8020000e 60000 2a008e 8020000e
  //   60000 2a010e 8020000e 60000 2a018e 8020000e 60080 2a000e 8020000e 60080 24020800 adb1c 8020000e
  //   60080 2a010e 8020000e 60080 2a018e 8020000e 60000 4a0058 80401058 60000 4a00d8 80401058 60000 4a0158
  //   80401058 60000 4a01d8 80401058 60080 4a0058 80403058 60080 24020800 adb1c 80401058 60080 4a0158
  //   80403058 6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
endmodule

module uROM_C (
  input  [7:0] OpeCode,
  input  Load,
  input  Update,
  output [11:0] STEP_MON,
  output [31:0] CtrlSignal
);

  wire not_1_out;
  wire [9:0] rom_1_data;

  ROM #(.dataWidth(10)) rom_1 (.addr(OpeCode), .data(rom_1_data));  // open: sel
  not not_1 (not_1_out, Load);
  Counter #(.width(10), .max('h3ff)) counter_1 (
    .load(Load), .D(rom_1_data), .count(not_1_out), .Q(STEP_MON[9:0]), .clk(Update));  // open: carry, clr
  ROM #(.addrWidth(10), .dataWidth(32)) rom_2 (.addr(STEP_MON[9:0]), .data(CtrlSignal));  // open: sel

  assign STEP_MON[11:10] = 2'b00;

  // Notes on the sheet:
  //   2段にしてROM小さくした
  //   μOPEROM
  //   contents of rom_1 (hex, n*v repeats v):
  //   0 2 4 6 8 a c e 10 12 14 16 18 1a 1c 1e 20 24 28 2c 30 34 38 3c 40 44 48 4c 50 54 58 5c 60 64 68 6c
  //   70 74 78 7c 80 84 88 8c 90 94 98 9c a0 a1 a2 a3 a4 a5 a6 a7 a8 a9 aa ab ac ad ae af b0 b1 b2 b3 b4
  //   b5 b6 b7 b8 b9 ba bb bc bd be bf c0 c2 c4 c6 c8 cb ce d1 d4 d6 d8 da dc dd de df e0 e6 ec ed ee f4
  //   fa 100 101 105 109 10b 10d 112 117 11c 121 124 127 12a 12d 133 137 13c 141 144 147 14a 14d 152 157
  //   15c 161 164 167 16a 16d 170 174 177 17a 17d 180 183 186 189 18d 190 193 196 199 19c 19f 1a2 1a6 1a9
  //   1ac 1af 1b2 1b5 1b8 1bb 1bf 1c2 1c5 1c8 1cb 1ce 1d1 1d4 1d8 1db 1de 1e1 1e4 1e7 1ea 1ed 1f1 1f4 1f7
  //   1fa 1fd 200 203 206 20a 20d 210 213 216 219 21c 21f 223 226 229 22b 22d 22f 231 233 235 237 239 23b
  //   23d 23f 241 243 245 247 249 24a 24b 24c 24d 24f 251 252 253 254 255 256 257 259 25b 25c 25d 25f 261
  //   270 271 272 273 274 275 276 277 278 279 287 295 298 299 29a 29b 29c 29d 2a0 2a3 2a6 2a9 2af 2b5 2bf
  //   2c0 2c1 2ca 2cf
  //   contents of rom_2 (hex, n*v repeats v):
  //   2402000c 80121300 2402000c 80123300 2402000c 80125300 2402000c 80127300 2402040c 80121300 2402040c
  //   80123300 2402040c 80125300 2402040c 80127300 3802000c 80020000 3802008c 80020000 3802010c 80020000
  //   3802018c 80020000 3802040c 80020000 3802048c 80020000 3802050c 80020000 3802058c 80020000 2402080c
  //   6db1c 24020304 80121300 2402080c 6db1c 24020304 80123300 2402080c 6db1c 24020304 80125300 2402080c
  //   6db1c 24020304 80127300 2402080c 6db1c 24020704 80121300 2402080c 6db1c 24020704 80123300 2402080c
  //   6db1c 24020704 80125300 2402080c 6db1c 24020704 80127300 2402080c 6db1c 38020004 80020000 2402080c
  //   6db1c 38020084 80020000 2402080c 6db1c 38020104 80020000 2402080c 6db1c 38020184 80020000 2402080c
  //   6db1c 38020404 80020000 2402080c 6db1c 38020484 80020000 2402080c 6db1c 38020504 80020000 2402080c
  //   6db1c 38020584 80020000 2402080c 6db1c 24020c04 80121300 2402080c 6db1c 24020c04 80123300 2402080c
  //   6db1c 24020c04 80125300 2402080c 6db1c 24020c04 80127300 2402040c 121300 2402041c 80123300 2402040c
  //   125300 2402041c 80127300 2402040c 121300 2402041c 80123300 2402040c 125300 2402041c 80127300
  //   2402080c 6db1c 38020c04 80020000 2402080c 6db1c 38020c84 80020000 2402080c 6db1c 38020d04 80020000
  //   2402080c 6db1c 38020d84 80020000 3802040c 20000 3802049c 80020000 3802050c 20000 3802059c 80020000
  //   3802040c 20000 3802049c 80020000 3802050c 20000 3802059c 17*80020000 80021100 80021180 80023100
  //   80023180 80025000 80025080 80027000 80027080 80021080 80023000 80025180 80027180 8002d00c 8002f00c
  //   8002d40c 8002f40c 21200 80023280 21600 80023680 23200 80025280 23600 80025680 60000 a0080 80029020
  //   60000 a0080 8002b020 60080 a0100 80029020 60080 a0100 8002b020 21200 80023280 21600 80023680 23200
  //   80025280 23600 80025680 80029800 80029c00 8002b800 8002bc00 2002fc08 18020000 20000 2002fc08
  //   18020080 80000000 2002fc08 18020200 20000 2002fc08 18020280 80000000 0 0 2002fc08 18020280 20000
  //   2002fc08 18020200 80000000 2002fc08 18020680 20000 2002fc08 18020600 80000000 2002fc08 18020a80
  //   20000 2002fc08 18020a00 80000000 0 24021f0c 2fc1c 24023f0c 8002fc1c 24025f0c 2fc1c 24027f0c 8002fc1c
  //   260015 80203015 260115 80207015 24020c0c 6ff1c 24020c0c aff1c 80029020 24020c0c 6ff1c 24020c0c aff1c
  //   8002b020 24020c0c 6ff1c 24020c0c aff1c 8002d020 24020c0c 6ff1c 24020c0c aff1c 8002f020 60000 a0080
  //   80029000 60000 a0080 8002b400 60400 a0100 80029000 60400 a0100 8002b400 60000 21100 425068 60080
  //   23180 80427068 60200 a0280 2940c 8002b020 60000 a0080 25200 27280 80029020 60100 a0180 25600 27680
  //   8002b020 2402080c 121000 8002db1c 2402080c 123000 8002db1c 2402080c 125000 8002db1c 2402080c 127000
  //   8002db1c 2402080c 6db1c 2402080c adb1c 80029020 2402080c 6db1c 2402080c adb1c 8002b020 2402080c
  //   6db1c 2402080c adb1c 8002d020 2402080c 6db1c 2402080c adb1c 8002f020 60000 2a0033 80201033 60000
  //   2a00b3 80201033 60000 2a0133 80201033 60000 2a01b3 80201033 60080 2a0033 80203033 60080 24020800
  //   adb1c 80201033 60080 2a0133 80203033 60080 2a01b3 80203033 60000 2a000e 8020100e 60000 2a008e
  //   8020100e 60000 2a010e 8020100e 60000 2a018e 8020100e 60080 2a000e 8020300e 60080 24020800 adb1c
  //   8020100e 60080 2a010e 8020300e 60080 2a018e 8020300e 60000 2a0030 80201030 60000 2a00b0 80201030
  //   60000 2a0130 80201030 60000 2a01b0 80201030 60080 2a0030 80203030 60080 24020800 adb1c 80201030
  //   60080 2a0130 80203030 60080 2a01b0 80203030 60000 2a000c 8020100c 60000 2a008c 8020100c 60000 2a010c
  //   8020100c 60000 2a018c 8020100c 60080 2a000c 8020300c 60080 24020800 adb1c 8020100c 60080 2a010c
  //   8020300c 60080 2a018c 8020300c 60000 4a0060 80401060 60000 4a00e0 80401060 60000 4a0160 80401060
  //   60000 4a01e0 80401060 60080 4a0060 80403060 60080 24020800 adb1c 80401060 60080 4a0160 80403060
  //   60080 4a01e0 80403060 60000 2a000e 8020000e 60000 2a008e 8020000e 60000 2a010e 8020000e 60000 2a018e
  //   8020000e 60080 2a000e 8020000e 60080 24020800 adb1c 8020000e 60080 2a010e 8020000e 60080 2a018e
  //   8020000e 60000 4a0058 80401058 60000 4a00d8 80401058 60000 4a0158 80401058 60000 4a01d8 80401058
  //   60080 4a0058 80403058 60080 24020800 adb1c 80401058 60080 4a0158 80403058 60080 4a01d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
endmodule

module uROM_D (
  input  [7:0] OpeCode,
  input  Load,
  input  Update,
  input  DOutClk,
  output [11:0] STEP_MON,
  output [31:0] CtrlSignal
);

  wire not_1_out;
  wire [9:0] register_1_q, rom_1_data;

  ROM #(.dataWidth(10)) rom_1 (.addr(OpeCode), .data(rom_1_data));  // open: sel
  not not_1 (not_1_out, Load);
  Counter #(.width(10), .max('h3ff)) counter_1 (
    .load(Load), .D(rom_1_data), .count(not_1_out), .Q(STEP_MON[9:0]), .clk(Update));  // open: carry, clr
  Register #(.width(10)) register_1 (.D(STEP_MON[9:0]), .Q(register_1_q), .clk(DOutClk));  // open: en, clr
  ROM #(.addrWidth(10), .dataWidth(32)) rom_2 (.addr(register_1_q), .data(CtrlSignal));  // open: sel

  assign STEP_MON[11:10] = 2'b00;

  // Notes on the sheet:
  //   2段にしてROM小さくした
  //   μOPEROM
  //   contents of rom_1 (hex, n*v repeats v):
  //   0 2 4 6 8 a c e 10 12 14 16 18 1a 1c 1e 20 24 28 2c 30 34 38 3c 40 44 48 4c 50 54 58 5c 60 64 68 6c
  //   70 74 78 7c 80 84 88 8c 90 94 98 9c a0 a1 a2 a3 a4 a5 a6 a7 a8 a9 aa ab ac ad ae af b0 b1 b2 b3 b4
  //   b5 b6 b7 b8 b9 ba bb bc bd be bf c0 c2 c4 c6 c8 cb ce d1 d4 d6 d8 da dc dd de df e0 e6 ec ef f2 f7
  //   fc 101 104 10a 110 112 114 119 11e 123 128 12b 12e 131 134 13a 13e 143 148 14b 14e 151 154 159 15e
  //   163 168 16b 16e 171 174 177 17b 17e 181 184 187 18a 18d 190 194 197 19a 19d 1a0 1a3 1a6 1a9 1ad 1b0
  //   1b3 1b6 1b9 1bc 1bf 1c2 1c6 1c9 1cc 1cf 1d2 1d5 1d8 1db 1df 1e2 1e5 1e8 1eb 1ee 1f1 1f4 1f8 1fb 1fe
  //   201 204 207 20a 20d 211 214 217 21a 21d 220 223 226 22a 22d 230 232 234 236 238 23a 23c 23e 240 242
  //   244 246 248 24a 24c 24e 250 251 252 253 254 256 258 25a 25c 25d 25e 25f 260 262 264 265 266 268 26a
  //   278 279 27a 27b 27c 27d 27e 27f 280 281 28b 297 29a 29b 29c 29d 29e 29f 2a2 2a5 2a8 2ab 2b1 2b7 2c0
  //   2c1 2c5 2ce 2d3
  //   contents of rom_2 (hex, n*v repeats v):
  //   2402000c 80121300 2402000c 80123300 2402000c 80125300 2402000c 80127300 2402040c 80121300 2402040c
  //   80123300 2402040c 80125300 2402040c 80127300 3802000c 80020000 3802008c 80020000 3802010c 80020000
  //   3802018c 80020000 3802040c 80020000 3802048c 80020000 3802050c 80020000 3802058c 80020000 2402080c
  //   6db1c 24020304 80121300 2402080c 6db1c 24020304 80123300 2402080c 6db1c 24020304 80125300 2402080c
  //   6db1c 24020304 80127300 2402080c 6db1c 24020704 80121300 2402080c 6db1c 24020704 80123300 2402080c
  //   6db1c 24020704 80125300 2402080c 6db1c 24020704 80127300 2402080c 6db1c 38020004 80020000 2402080c
  //   6db1c 38020084 80020000 2402080c 6db1c 38020104 80020000 2402080c 6db1c 38020184 80020000 2402080c
  //   6db1c 38020404 80020000 2402080c 6db1c 38020484 80020000 2402080c 6db1c 38020504 80020000 2402080c
  //   6db1c 38020584 80020000 2402080c 6db1c 24020c04 80121300 2402080c 6db1c 24020c04 80123300 2402080c
  //   6db1c 24020c04 80125300 2402080c 6db1c 24020c04 80127300 2402040c 121300 2402041c 80123300 2402040c
  //   125300 2402041c 80127300 2402040c 121300 2402041c 80123300 2402040c 125300 2402041c 80127300
  //   2402080c 6db1c 38020c04 80020000 2402080c 6db1c 38020c84 80020000 2402080c 6db1c 38020d04 80020000
  //   2402080c 6db1c 38020d84 80020000 3802040c 20000 3802049c 80020000 3802050c 20000 3802059c 80020000
  //   3802040c 20000 3802049c 80020000 3802050c 20000 3802059c 17*80020000 80021100 80021180 80023100
  //   80023180 80025000 80025080 80027000 80027080 80021080 80023000 80025180 80027100 8002d00c 8002f00c
  //   8002d40c 8002f40c 21200 80023280 21600 80023680 23200 80025280 23600 80025680 60000 a0080 80029020
  //   60000 a0080 8002b020 60080 a0100 80029020 60080 a0100 8002b020 21200 80023280 21600 80023680 23200
  //   80025280 23600 80025680 80029800 80029c00 8002b800 8002bc00 2002fc08 18020080 20000 2002fc08
  //   18020000 80000000 2002fc08 18020280 20000 2002fc08 18020200 80000000 60000 21080 80423068 60100
  //   25180 80427068 2002fc08 18020280 2002fc08 18020200 80000000 2002fc08 18020680 2002fc08 18020600
  //   80000000 2002fc08 18020a80 2002fc08 18020a00 80000000 2402080c 6db1c 8002fc04 24020f0c 121f0c 2fc1c
  //   24020f0c 123f0c 8002fc1c 24020f0c 125f0c 2fc1c 24020f0c 127f0c 8002fc1c 260015 80203015 260115
  //   80207015 24020c0c 6ff1c 24020c0c aff1c 80029020 24020c0c 6ff1c 24020c0c aff1c 8002b020 24020c0c
  //   6ff1c 24020c0c aff1c 8002d020 24020c0c 6ff1c 24020c0c aff1c 8002f020 60000 a0080 80029000 60000
  //   a0080 8002b400 60400 a0100 80029000 60400 a0100 8002b400 60000 21100 425068 60080 23180 80427068
  //   60200 a0280 2940c 8002b020 60000 a0080 25200 27280 80029020 60100 a0180 25600 27680 8002b020
  //   2402080c 121300 8002d81c 2402080c 123300 8002d81c 2402080c 125300 8002d81c 2402080c 127300 8002d81c
  //   2402080c 6db1c 2402080c adb1c 80029020 2402080c 6db1c 2402080c adb1c 8002b020 2402080c 6db1c
  //   2402080c adb1c 8002d020 2402080c 6db1c 2402080c adb1c 8002f020 60000 2a0033 80201033 60000 2a00b3
  //   80201033 60000 2a0133 80201033 60000 2a01b3 80201033 60080 2a0033 80203033 60000 2402080c adb1c
  //   80201033 60080 2a0133 80203033 60080 2a01b3 80203033 60000 2a000e 8020100e 60000 2a008e 8020100e
  //   60000 2a010e 8020100e 60000 2a018e 8020100e 60080 2a000e 8020300e 60000 2402080c adb1c 8020100e
  //   60080 2a010e 8020300e 60080 2a018e 8020300e 60000 2a0030 80201030 60000 2a00b0 80201030 60000 2a0130
  //   80201030 60000 2a01b0 80201030 60080 2a0030 80203030 60000 2402080c adb1c 80201030 60080 2a0130
  //   80203030 60080 2a01b0 80203030 60000 2a000c 8020100c 60000 2a008c 8020100c 60000 2a010c 8020100c
  //   60000 2a018c 8020100c 60080 2a000c 8020300c 60000 2402080c adb1c 8020100c 60080 2a010c 8020300c
  //   60080 2a018c 8020300c 60000 4a0060 80401060 60000 4a00e0 80401060 60000 4a0160 80401060 60000 4a01e0
  //   80401060 60080 4a0060 80403060 60000 2402080c adb1c 80401060 60080 4a0160 80403060 60080 4a01e0
  //   80403060 60000 2a000e 8020000e 60000 2a008e 8020000e 60000 2a010e 8020000e 60000 2a018e 8020000e
  //   60080 2a000e 8020000e 60000 2402080c adb1c 8020000e 60080 2a010e 8020000e 60080 2a018e 8020000e
  //   60000 4a0058 80401058 60000 4a00d8 80401058 60000 4a0158 80401058 60000 4a01d8 80401058 60080 4a0058
  //   80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
endmodule

module ACU (
  input  [15:0] A,
  input  [15:0] B,
  input  [31:0] ctrl,
  output [15:0] Y
);
endmodule

// Mux
module AddrExMux (
  input  [7:0] A,
  input  B,
  input  Sel,
  output [7:0] Y
);

  Multiplexer #(.width(8), .disabled(0), .enable("false")) multiplexer_1 (.in0(A), .in1({8{B}}), .out(Y), .sel(Sel));
endmodule

module ALU (
  input  [15:0] S,
  input  [7:0] B,
  input  [7:0] A,
  input  [4:0] fromFLAG,
  input  [9:0] fromDAA,
  output [4:0] toFLAG,
  output [9:0] toDAA,
  output [7:0] ALU_OUT
);

  wire alu8a_1_cy;
  wire [7:0] alu8a_1_y, alu8l_1_y, multiplexer_1_out, multiplexer_3_out;
  wire [7:7] undriven;

  Multiplexer #(.width(8), .disabled(0), .enable("false")) multiplexer_1 (
    .in0(A), .in1(8'h38), .out(multiplexer_1_out), .sel(S[9]));
  ALU8L alu8l_1 (.A(multiplexer_1_out), .B(B), .S(S[7:4]), .Y(alu8l_1_y));
  ALU8A alu8a_1 (.B(alu8l_1_y), .A(multiplexer_1_out), .Cin(S[10]), .CY(alu8a_1_cy), .Y(alu8a_1_y));  // open: AC
  Multiplexer #(.select(2), .disabled(0), .enable("false")) multiplexer_2 (
    .in0(alu8a_1_cy), .in1(multiplexer_1_out[0]), .in3(fromDAA[1]), .out(toFLAG[0]), .sel(S[1:0]));  // open: in2
  Multiplexer #(.select(2), .width(8), .disabled(0), .enable("false")) multiplexer_3 (
    .in0(alu8a_1_y), .in1(alu8l_1_y), .in2({undriven[7], multiplexer_1_out[7:1]}),
    .in3({multiplexer_1_out[6:0], S[10]}), .out(multiplexer_3_out), .sel(S[3:2]));
  Multiplexer #(.width(8), .disabled(0), .enable("false")) multiplexer_4 (
    .in0(multiplexer_3_out), .in1(fromDAA[9:2]), .out(ALU_OUT), .sel(S[8]));
endmodule

module ALU8L (
  input  [7:0] A,
  input  [7:0] B,
  input  [3:0] S,
  output [7:0] Y
);

  Multiplexer #(.select(2), .disabled(0), .enable("false")) multiplexer_1 (
    .in0(S[0]), .in1(S[1]), .in2(S[2]), .in3(S[3]), .out(Y[4]), .sel({B[4], A[4]}));
  Multiplexer #(.select(2), .disabled(0), .enable("false")) multiplexer_2 (
    .in0(S[0]), .in1(S[1]), .in2(S[2]), .in3(S[3]), .out(Y[5]), .sel({B[5], A[5]}));
  Multiplexer #(.select(2), .disabled(0), .enable("false")) multiplexer_3 (
    .in0(S[0]), .in1(S[1]), .in2(S[2]), .in3(S[3]), .out(Y[6]), .sel({B[6], A[6]}));
  Multiplexer #(.select(2), .disabled(0), .enable("false")) multiplexer_4 (
    .in0(S[0]), .in1(S[1]), .in2(S[2]), .in3(S[3]), .out(Y[7]), .sel({B[7], A[7]}));
  Multiplexer #(.select(2), .disabled(0), .enable("false")) multiplexer_5 (
    .in0(S[0]), .in1(S[1]), .in2(S[2]), .in3(S[3]), .out(Y[0]), .sel({B[0], A[0]}));
  Multiplexer #(.select(2), .disabled(0), .enable("false")) multiplexer_6 (
    .in0(S[0]), .in1(S[1]), .in2(S[2]), .in3(S[3]), .out(Y[1]), .sel({B[1], A[1]}));
  Multiplexer #(.select(2), .disabled(0), .enable("false")) multiplexer_7 (
    .in0(S[0]), .in1(S[1]), .in2(S[2]), .in3(S[3]), .out(Y[2]), .sel({B[2], A[2]}));
  Multiplexer #(.select(2), .disabled(0), .enable("false")) multiplexer_8 (
    .in0(S[0]), .in1(S[1]), .in2(S[2]), .in3(S[3]), .out(Y[3]), .sel({B[3], A[3]}));
endmodule

module ALU4A (
  input  [3:0] B,
  input  [3:0] A,
  input  CIn,
  output COut,
  output [3:0] Y
);

  wire and_1_out, and_2_out, and_3_out, and_4_out, and_5_out, and_6_out, and_7_out, and_8_out, and_9_out,
       and_10_out, and_11_out, and_12_out, and_13_out, and_14_out, or_2_out, or_3_out, or_4_out, xor_1_out,
       xor_2_out, xor_3_out, xor_4_out;

  xor xor_1 (xor_1_out, B[3], A[3]);
  and and_1 (and_1_out, B[3], A[3]);
  xor xor_2 (xor_2_out, B[2], A[2]);
  and and_2 (and_2_out, B[2], A[2]);
  xor xor_3 (xor_3_out, B[1], A[1]);
  and and_3 (and_3_out, B[1], A[1]);
  xor xor_4 (xor_4_out, B[0], A[0]);
  and and_4 (and_4_out, B[0], A[0]);
  and and_5 (and_5_out, xor_1_out, and_2_out);
  and and_6 (and_6_out, xor_1_out, xor_2_out, and_3_out);
  and and_7 (and_7_out, xor_1_out, xor_2_out, xor_3_out, and_4_out);
  and and_8 (and_8_out, xor_1_out, xor_2_out, xor_3_out, xor_4_out, CIn);
  and and_9 (and_9_out, xor_2_out, and_3_out);
  and and_10 (and_10_out, xor_2_out, xor_3_out, and_4_out);
  and and_11 (and_11_out, xor_2_out, xor_3_out, xor_4_out, CIn);
  and and_12 (and_12_out, xor_3_out, and_4_out);
  and and_13 (and_13_out, xor_3_out, xor_4_out, CIn);
  and and_14 (and_14_out, xor_4_out, CIn);
  or or_1 (COut, and_1_out, and_5_out, and_6_out, and_7_out, and_8_out);
  or or_2 (or_2_out, and_2_out, and_9_out, and_10_out, and_11_out);
  or or_3 (or_3_out, and_3_out, and_12_out, and_13_out);
  or or_4 (or_4_out, and_4_out, and_14_out);
  xor xor_5 (Y[3], xor_1_out, or_2_out);
  xor xor_6 (Y[2], xor_2_out, or_3_out);
  xor xor_7 (Y[1], xor_3_out, or_4_out);
  xor xor_8 (Y[0], xor_4_out, CIn);
endmodule

module ALU8A (
  input  [7:0] B,
  input  [7:0] A,
  input  Cin,
  output CY,
  output [7:0] Y,
  output AC
);

  ALU4A alu4a_1 (.B(B[7:4]), .A(A[7:4]), .CIn(AC), .COut(CY), .Y(Y[7:4]));
  ALU4A alu4a_2 (.B(B[3:0]), .A(A[3:0]), .CIn(Cin), .COut(AC), .Y(Y[3:0]));
endmodule

module CarrySelector (
  input  CY,
  input  A7,
  input  OP0,
  input  OP1,
  output CC
);

  Multiplexer #(.select(2), .enable("false")) multiplexer_1 (
    .in0(CY), .in1(A7), .in2(1'b1), .in3(1'b0), .out(CC), .sel({OP1, OP0}));
endmodule

module ZeroFlag (
  input  [7:0] A,
  output Y
);

  nor nor_1 (Y, A[0], A[1], A[2], A[3], A[4], A[5], A[6], A[7]);
endmodule

module ALU_OP (
  input  D,
  input  C,
  input  B,
  input  A,
  output op3,
  output op2,
  output op1,
  output op0
);

  wire and_1_out, and_2_out, and_3_out, and_4_out, and_5_out, and_6_out, and_7_out, and_8_out, and_9_out,
       and_10_out, not_1_out, not_2_out, not_3_out, not_4_out;

  not not_1 (not_1_out, D);
  not not_2 (not_2_out, C);
  not not_3 (not_3_out, B);
  not not_4 (not_4_out, A);
  and and_1 (and_1_out, not_1_out, not_2_out, not_3_out);
  and and_2 (and_2_out, C, not_4_out);
  and and_3 (and_3_out, D, A);
  and and_4 (and_4_out, not_3_out, A);
  and and_5 (and_5_out, C, B, not_4_out);
  and and_6 (and_6_out, C, A);
  and and_7 (and_7_out, D, A);
  and and_8 (and_8_out, not_2_out, B);
  and and_9 (and_9_out, B, A);
  and and_10 (and_10_out, D, A);
  or or_1 (op3, and_1_out, and_2_out, and_3_out);
  or or_2 (op2, and_1_out, and_4_out, and_5_out);
  or or_3 (op1, B, and_6_out, and_7_out);
  or or_4 (op0, and_8_out, and_9_out, and_10_out);
endmodule

module ADD_6 (
  input  a3,
  input  a2,
  input  a1,
  input  a0,
  input  ADD,
  output cy,
  output y3,
  output y2,
  output y1,
  output y0
);

  wire and_1_out, and_2_out, and_3_out, and_5_out, and_6_out, and_7_out, and_8_out, and_9_out, and_10_out,
       not_1_out, not_2_out, not_3_out, not_4_out, not_5_out, or_1_out, or_2_out;

  or or_1 (or_1_out, a2, a3);
  not not_1 (not_1_out, a3);
  not not_2 (not_2_out, a3);
  not not_3 (not_3_out, a1);
  not not_4 (not_4_out, a1);
  and and_1 (and_1_out, not_1_out, a1);
  and and_2 (and_2_out, not_2_out, not_3_out);
  and and_3 (and_3_out, a2, a1);
  or or_2 (or_2_out, and_2_out, and_3_out);
  not not_5 (not_5_out, ADD);
  and and_4 (cy, or_1_out, ADD);
  and and_5 (and_5_out, ADD, and_1_out);
  and and_6 (and_6_out, not_5_out, a3);
  and and_7 (and_7_out, ADD, or_2_out);
  and and_8 (and_8_out, not_5_out, a2);
  and and_9 (and_9_out, ADD, not_4_out);
  and and_10 (and_10_out, not_5_out, a1);
  or or_3 (y3, and_5_out, and_6_out);
  or or_4 (y2, and_7_out, and_8_out);
  or or_5 (y1, and_9_out, and_10_out);

  assign y0 = a0;
endmodule

// INC
module _4bit_addc_0 (
  input  cin,
  input  a3,
  input  a2,
  input  a1,
  input  a0,
  output y3,
  output y2,
  output y1,
  output y0
);

  wire and_1_out, and_2_out, and_3_out, and_4_out, and_5_out, and_6_out, and_7_out, and_8_out, and_9_out,
       and_10_out, and_11_out, and_12_out, and_13_out, and_14_out, not_1_out, not_2_out, not_3_out,
       not_4_out, not_5_out;

  not not_1 (not_1_out, cin);
  not not_2 (not_2_out, a3);
  not not_3 (not_3_out, a2);
  not not_4 (not_4_out, a1);
  not not_5 (not_5_out, a0);
  and and_1 (and_1_out, not_1_out, a3);
  and and_2 (and_2_out, a3, not_3_out);
  and and_3 (and_3_out, a3, not_4_out);
  and and_4 (and_4_out, a3, not_5_out);
  and and_5 (and_5_out, cin, not_2_out, a2, a1, a0);
  and and_6 (and_6_out, not_1_out, a2);
  and and_7 (and_7_out, a2, not_4_out);
  and and_8 (and_8_out, a2, not_5_out);
  and and_9 (and_9_out, cin, not_3_out, a1, a0);
  and and_10 (and_10_out, not_1_out, a1);
  and and_11 (and_11_out, a1, not_5_out);
  and and_12 (and_12_out, cin, not_4_out, a0);
  and and_13 (and_13_out, not_1_out, a0);
  and and_14 (and_14_out, cin, not_5_out);
  or or_1 (y3, and_1_out, and_2_out, and_3_out, and_4_out, and_5_out);
  or or_2 (y2, and_6_out, and_7_out, and_8_out, and_9_out);
  or or_3 (y1, and_10_out, and_11_out, and_12_out);
  or or_4 (y0, and_13_out, and_14_out);
endmodule

module DAA (
  input  [7:0] A,
  input  AC,
  input  Cin,
  output AC_2,
  output [7:0] Y,
  output Cout
);

  wire and_2_out, GT9_hi, GT9_lo, n4bit_addc_0_1_y0, n4bit_addc_0_1_y1, n4bit_addc_0_1_y2, n4bit_addc_0_1_y3,
       or_1_out, or_2_out, or_3_out;

  // Probe on A
  or or_1 (or_1_out, A[1], A[2]);
  and and_1 (GT9_lo, or_1_out, A[3]);
  or or_2 (or_2_out, GT9_lo, AC);
  ADD_6 add_6_1 (
    .a3(A[3]), .cy(AC_2), .a2(A[2]), .y3(Y[3]), .a1(A[1]), .y2(Y[2]), .y1(Y[1]), .a0(A[0]), .y0(Y[0]),
    .ADD(or_2_out));
  _4bit_addc_0 u_4bit_addc_0_1 (
    .cin(AC_2), .a3(A[7]), .a2(A[6]), .y3(n4bit_addc_0_1_y3), .a1(A[5]), .a0(A[4]), .y2(n4bit_addc_0_1_y2),
    .y1(n4bit_addc_0_1_y1), .y0(n4bit_addc_0_1_y0));
  and and_2 (and_2_out, AC_2, A[4]);
  or or_3 (or_3_out, and_2_out, A[5], A[6]);
  // Probe on Y
  ADD_6 add_6_2 (
    .a3(n4bit_addc_0_1_y3), .a2(n4bit_addc_0_1_y2), .y3(Y[7]), .a1(n4bit_addc_0_1_y1), .y2(Y[6]), .y1(Y[5]),
    .a0(n4bit_addc_0_1_y0), .y0(Y[4]), .ADD(Cout));  // open: cy
  and and_3 (GT9_hi, or_3_out, A[7]);
  or or_4 (Cout, Cin, GT9_hi);

  // Notes on the sheet:
  //   i8080Aは、このときのフラグがACに書き戻されるのだと思う 
endmodule

module TEMP_REG (
  input  [7:0] fromDBUS,
  input  [11:0] ctrl,
  output [7:0] monitor,
  output [7:0] toALU
);

  wire [7:0] multiplexer_1_out;

  Register register_1 (.D(fromDBUS), .en(ctrl[9]), .Q(monitor), .clk(ctrl[10]));  // open: clr
  assign toALU = ctrl[8] ? multiplexer_1_out : 8'bz;  // Controlled_Buffer controlled_buffer_1
  Multiplexer #(.width(8), .disabled(0), .enable("false")) multiplexer_1 (
    .in0(monitor), .in1(fromDBUS), .out(multiplexer_1_out), .sel(ctrl[11]));
endmodule

module ACC (
  input  [7:0] fromDATA_BUS,
  input  [11:0] ctrl,
  output [7:0] Monitor,
  output [7:0] toACT,
  output [7:0] toDATA_BUS,
  output [7:0] THRU
);

  Register register_1 (.D(fromDATA_BUS), .en(ctrl[1]), .Q(Monitor), .clk(ctrl[0]));  // open: clr
  Multiplexer #(.width(8), .disabled(0), .enable("false")) multiplexer_1 (
    .in0(Monitor), .in1(fromDATA_BUS), .out(toACT), .sel(ctrl[2]));
  assign toDATA_BUS = ctrl[3] ? toACT : 8'bz;  // Controlled_Buffer controlled_buffer_1

  assign THRU = fromDATA_BUS;
endmodule

module ACT (
  input  [7:0] fromAcc,
  input  [7:0] AccTHRU,
  input  [11:0] ctrl,
  output [7:0] Monitor,
  output [7:0] toALU
);

  wire undriven, undriven_2, undriven_3;
  wire [7:0] multiplexer_1_out;

  Multiplexer #(.width(8), .disabled(0), .enable("false")) multiplexer_1 (
    .in0(fromAcc), .in1(AccTHRU), .out(multiplexer_1_out));  // open: sel
  Register register_1 (.D(multiplexer_1_out), .en(undriven_2), .Q(Monitor), .clk(undriven));  // open: clr
  Multiplexer #(.width(8), .disabled(0), .enable("false")) multiplexer_2 (
    .in0(Monitor), .in1(multiplexer_1_out), .out(toALU), .sel(undriven_3));
endmodule

module TMP (
  input  [7:0] fromAcc,
  input  Latch,
  input  clk,
  input  OutEn_Thru,
  output [7:0] toALU
);

  wire [7:0] register_1_q;

  Register register_1 (.D(fromAcc), .en(Latch), .Q(register_1_q), .clk(clk));  // open: clr
  Multiplexer #(.width(8), .disabled(0), .enable("false")) multiplexer_1 (
    .in0(register_1_q), .in1(fromAcc), .out(toALU), .sel(OutEn_Thru));
endmodule

module Carry (
  input  CarryIn,
  input  [1:0] CarryOutCtrl,
  input  [1:0] CarryInCtrl,
  input  CarrySrcSel,
  input  fromALU,
  output CarryOut,
  output toALU
);

  wire multiplexer_2_out, not_1_out, not_2_out;

  not not_1 (not_1_out, multiplexer_2_out);
  Multiplexer #(.select(2), .disabled(0), .enable("false")) multiplexer_1 (
    .in0(multiplexer_2_out), .in1(not_1_out), .in2(1'b1), .in3(1'b0), .out(CarryOut), .sel(CarryOutCtrl));
  Multiplexer #(.disabled(0), .enable("false")) multiplexer_2 (
    .in0(toALU), .in1(fromALU), .out(multiplexer_2_out), .sel(CarrySrcSel));
  Multiplexer #(.select(2), .disabled(0), .enable("false")) multiplexer_3 (
    .in0(CarryIn), .in1(not_2_out), .in2(1'b1), .in3(1'b0), .out(toALU), .sel(CarryInCtrl));
  not not_2 (not_2_out, CarryIn);
endmodule

module Flag_Flip_Flop (
  input  [1:0] CarryOutCtrl,
  input  [1:0] CarryInCtrl,
  input  CarrySrcSel,
  input  fromALU,
  output toALU
);

  wire CY_q, multiplexer_1_out, multiplexer_2_out, not_1_out, not_2_out, undriven;

  not not_1 (not_1_out, multiplexer_2_out);
  Multiplexer #(.select(2), .disabled(0), .enable("false")) multiplexer_1 (
    .in0(multiplexer_2_out), .in1(not_1_out), .in2(1'b1), .in3(1'b0), .out(multiplexer_1_out),
    .sel(CarryOutCtrl));
  Register #(.width(4)) Flags ();  // open: D, en, Q, clk, clr
  Multiplexer #(.disabled(0), .enable("false")) multiplexer_2 (
    .in0(toALU), .in1(fromALU), .out(multiplexer_2_out), .sel(CarrySrcSel));
  Register #(.width(1)) CY (.D(undriven), .Q(CY_q));  // open: en, clk, clr
  Multiplexer #(.select(2), .disabled(0), .enable("false")) multiplexer_3 (
    .in0(undriven), .in1(not_2_out), .in2(1'b1), .in3(1'b0), .out(toALU), .sel(CarryInCtrl));
  not not_2 (not_2_out, undriven);
endmodule

module ClockDiv (
  input  CLK,
  output P2,
  output P1
);

  wire d_ff_1_q, d_ff_2_q, d_ff_3_q, d_ff_4_q, div9_1_y0, div9_1_y1, div9_1_y2, div9_1_y3, n2layerclock_1_p1,
       n2layerclock_1_p2, not_1_out;

  Div9 div9_1 (
    .A3(d_ff_4_q), .A2(d_ff_3_q), .A1(d_ff_2_q), .A0(d_ff_1_q), .Y3(div9_1_y3), .Y2(div9_1_y2),
    .Y1(div9_1_y1), .Y0(div9_1_y0));
  D_Flip_Flop d_ff_1 (.clk(CLK), .D(div9_1_y0), .Q(d_ff_1_q));  // open: Qn, preset, en, reset
  D_Flip_Flop d_ff_2 (.clk(CLK), .D(div9_1_y1), .Q(d_ff_2_q));  // open: Qn, preset, en, reset
  D_Flip_Flop d_ff_3 (.clk(CLK), .D(div9_1_y2), .Q(d_ff_3_q));  // open: Qn, preset, en, reset
  D_Flip_Flop d_ff_4 (.clk(CLK), .D(div9_1_y3), .Q(d_ff_4_q));  // open: Qn, preset, en, reset
  not not_1 (not_1_out, CLK);
  _2layerClock u_2layerclock_1 (
    .A3(d_ff_4_q), .A2(d_ff_3_q), .A1(d_ff_2_q), .A0(d_ff_1_q), .P2(n2layerclock_1_p2), .P1(n2layerclock_1_p1));
  D_Flip_Flop d_ff_5 (.clk(not_1_out), .D(n2layerclock_1_p2), .Q(P2));  // open: Qn, preset, en, reset
  D_Flip_Flop d_ff_6 (.clk(not_1_out), .D(n2layerclock_1_p1), .Q(P1));  // open: Qn, preset, en, reset
endmodule

module Div9 (
  input  A3,
  input  A2,
  input  A1,
  input  A0,
  output Y3,
  output Y2,
  output Y1,
  output Y0
);

  wire and_2_out, and_3_out, and_4_out, and_5_out, and_6_out, not_1_out, not_2_out, not_3_out, not_4_out;

  not not_1 (not_1_out, A3);
  not not_2 (not_2_out, A2);
  not not_3 (not_3_out, A1);
  not not_4 (not_4_out, A0);
  and and_1 (Y3, not_1_out, A2, A1, A0);
  and and_2 (and_2_out, not_1_out, not_2_out, A1, A0);
  and and_3 (and_3_out, not_1_out, A2, not_3_out);
  and and_4 (and_4_out, not_1_out, A2, not_4_out);
  and and_5 (and_5_out, not_1_out, not_3_out, A0);
  and and_6 (and_6_out, not_1_out, A1, not_4_out);
  and and_7 (Y0, not_1_out, not_4_out);
  or or_1 (Y2, and_2_out, and_3_out, and_4_out);
  or or_2 (Y1, and_5_out, and_6_out);
endmodule

module _2layerClock (
  input  A3,
  input  A2,
  input  A1,
  input  A0,
  output P2,
  output P1
);

  wire and_1_out, and_2_out, and_3_out, and_4_out, not_1_out, not_2_out, not_3_out, not_4_out;

  not not_1 (not_1_out, A3);
  not not_2 (not_2_out, A2);
  not not_3 (not_3_out, A1);
  not not_4 (not_4_out, A0);
  and and_1 (and_1_out, not_1_out, A1, A0);
  and and_2 (and_2_out, not_1_out, A2);
  and and_3 (and_3_out, not_1_out, not_2_out, not_3_out, A0);
  and and_4 (and_4_out, not_1_out, not_2_out, A1, not_4_out);
  or or_1 (P2, and_1_out, and_2_out);
  or or_2 (P1, and_3_out, and_4_out);
endmodule

module _8BitGPReg_H (
  input  [7:0] fromINCDEC,
  input  [7:0] fromDBUS,
  input  [7:0] Control,
  output [7:0] Monitor,
  output [7:0] toDBUS,
  output [7:0] toINCDEC,
  output out_7,
  output out_8,
  output [7:0] ctrlOut
);

  Register register_1 (.D(fromINCDEC), .en(Control[6]), .Q(Monitor), .clk(Control[7]));  // open: clr
  assign fromDBUS = Control[4] ? Monitor : 8'bz;  // Controlled_Buffer controlled_buffer_1

  assign ctrlOut = Control;
  assign out_7 = Control[4];
  assign out_8 = Control[6];
  assign toDBUS = fromINCDEC;
  assign toINCDEC = fromDBUS;
endmodule

module _8BitGPReg_L (
  input  [7:0] fromINCDEC,
  input  [7:0] fromDBUS,
  input  [7:0] Control,
  output [7:0] Monitor,
  output [7:0] toDBUS,
  output [7:0] toINCDEC,
  output out_7,
  output out_8
);

  Register register_1 (.D(fromINCDEC), .en(Control[5]), .Q(Monitor), .clk(Control[7]));  // open: clr
  assign fromDBUS = Control[3] ? Monitor : 8'bz;  // Controlled_Buffer controlled_buffer_1

  assign out_7 = Control[3];
  assign out_8 = Control[5];
  assign toDBUS = fromINCDEC;
  assign toINCDEC = fromDBUS;
endmodule

module TIMING_AND_CONTROL (
  input  nReset,
  input  P1,
  input  P2,
  input  IRQ,
  input  [31:0] in_5,
  output [11:0] AccCtrl,
  output ALUCtrl,
  output [31:0] ctrl,
  output [15:0] ALUctrl_2
);

  wire IRQ_t;

  not not_1 (IRQ_t, IRQ);

  assign ALUCtrl = 1'b0;

  // Other names for the same wires on the sheet: φ1 = P1; φ2 = P2

  // Notes on the sheet:
  //   nReset: pull=up
endmodule

// INC/DEC ADDRESS LATCH
module ADDRESS_LATCH (
  input  [7:0] LO,
  input  [7:0] HI,
  input  [31:0] ctrl,
  output [15:0] monitor,
  output [15:0] OUT,
  output out_6,
  output [7:0] INC_DEC_LO,
  output [7:0] INC_DEC_HI,
  output [15:0] monitor_2
);

  wire undriven;
  wire [15:0] adder_1_out, subtractor_1_out;

  Register #(.width(16)) register_1 (.D({HI, LO}), .en(out_6), .Q(OUT), .clk(undriven));  // open: clr
  Adder #(.width(16)) adder_1 (.a({HI, LO}), .b({16{1'b0}}), .out(adder_1_out), .cin(1'b1));  // open: cout
  Subtractor #(.width(16)) subtractor_1 (
    .a({HI, LO}), .b({16{1'b0}}), .out(subtractor_1_out), .bin(1'b1));  // open: bout
  Multiplexer #(.select(2), .width(16), .disabled(0), .enable("false")) multiplexer_1 (
    .in0({16{1'b0}}), .in1({HI, LO}), .in2(adder_1_out), .in3(subtractor_1_out),
    .out({INC_DEC_HI, INC_DEC_LO}), .sel(ctrl[31:30]));

  assign monitor = {HI, LO};
  assign monitor_2 = {INC_DEC_HI, INC_DEC_LO};
endmodule

module DATABUS_BUFFER (
  input  [7:0] fromExDataBus,
  input  [7:0] fromDataBus,
  input  [31:0] ctrl,
  output [7:0] monitor,
  output [7:0] toExDataBus,
  output [7:0] toDataBus
);

  wire [7:0] multiplexer_1_out;

  Multiplexer #(.width(8), .disabled(0), .enable("false")) multiplexer_1 (
    .in0(fromExDataBus), .out(multiplexer_1_out));  // open: in1, sel
  Register register_1 (.D(multiplexer_1_out), .Q(monitor));  // open: en, clk, clr
  Controlled_Buffer #(.width(8)) controlled_buffer_1 (.in(monitor), .out(toExDataBus));  // open: en

  // Other names for the same wires on the sheet: STATE[7:0] = ctrl[23:16]
endmodule

module REGISTER_SELECTOR (
  input  [31:0] ctrl,
  output [7:0] WZ_Ctrl,
  output [7:0] BC_Ctrl,
  output [7:0] DE_ctrl,
  output [7:0] HL_ctrl,
  output [7:0] SP_ctrl,
  output [7:0] PC_ctrl
);

  wire DH_Exchg_q, not_1_out;
  wire [3:0] multiplexer_1_out, multiplexer_2_out, undriven, undriven_2;

  D_Flip_Flop DH_Exchg (.Q(DH_Exchg_q));  // open: clk, D, Qn, preset, en, reset
  Multiplexer #(.width(4), .disabled(0), .enable("false")) multiplexer_1 (
    .in0(undriven), .in1(undriven_2), .out(multiplexer_1_out), .sel(DH_Exchg_q));
  not not_1 (not_1_out, DH_Exchg_q);
  Multiplexer #(.width(4), .disabled(0), .enable("false")) multiplexer_2 (
    .in0(undriven_2), .in1(undriven), .out(multiplexer_2_out), .sel(not_1_out));
endmodule

module MULTIPLEXER (
  input  [7:0] fromDATABUS,
  input  [7:0] fromREGISTER_ARRAY_hi,
  input  [7:0] fromREGISTER_ARRAY_lo,
  input  [31:0] ctrl,
  output [7:0] toDATABUS,
  output [7:0] toREGISTER_ARRAY_hi,
  output [7:0] toREGISTER_ARRAY_lo
);
endmodule

module DECIMAL_ADJUST (
  input  [9:0] fromALU,
  output [9:0] toALU
);

  DAA daa_1 (.A(fromALU[9:2]), .AC(fromALU[0]), .Cin(fromALU[1]), .AC_2(toALU[0]), .Y(toALU[9:2]), .Cout(toALU[1]));
endmodule

module INSTRUCTIN_REGISTER (
  input  [7:0] OPECODEin,
  input  [31:0] ctrl,
  output [7:0] monitor,
  output [15:0] OPECODEout
);

  Register register_1 (.D(OPECODEin), .en(ctrl[6]), .Q(monitor), .clk(ctrl[8]));  // open: clr

  assign OPECODEout = {OPECODEin, monitor};
endmodule

module FLAG (
  input  [7:0] fromDATABUS,
  input  [4:0] fromALU,
  input  [15:0] ctrl,
  output [7:0] toDATABUS,
  output [4:0] toALU
);
endmodule

module ADDRESS_BUFFER (
  input  [15:0] in_1,
  input  ctrl,
  output [15:0] out_3
);

  assign out_3 = ctrl ? in_1 : 16'bz;  // Controlled_Buffer controlled_buffer_1
endmodule

module StateCtrl (
  input  [4:0] state,
  input  [2:0] stateMode,
  output [4:0] next
);

  wire priority_encoder_1_gs;
  wire [2:0] priority_encoder_1_out, rom_1_data;

  ROM rom_1 (.addr({state, stateMode}), .data({next, rom_1_data}));  // open: sel
  Priority_Encoder priority_encoder_1 (
    .out(priority_encoder_1_out), .gs(priority_encoder_1_gs));  // open: in0, in1, in2, in3, in4, in5, in6, in7, en_in, en_out
  Multiplexer #(.select(3), .width(3), .disabled(0), .enable("false")) multiplexer_1 (.sel(priority_encoder_1_out));  // open: in0, in1, in2, in3, in4, in5, in6, in7, out
endmodule

module STATE_IND (
  input  [9:0] State_in,
  output out_2,
  output out_3,
  output out_4,
  output out_5,
  output out_6,
  output out_7,
  output out_8,
  output out_9,
  output out_10,
  output out_11
);


  assign out_2 = State_in[0];
  assign out_3 = State_in[1];
  assign out_4 = State_in[2];
  assign out_5 = State_in[3];
  assign out_6 = State_in[4];
  assign out_7 = State_in[5];
  assign out_8 = State_in[6];
  assign out_9 = State_in[7];
  assign out_10 = State_in[8];
  assign out_11 = State_in[9];
endmodule
